# Fritzing sketch diagram (saved by Fritzing 0.9.2b)
breadboards: 1

parts:
  Part1 = Arduino Uno (Rev3)
  U1 = TMP36 [package=to-92]
  S1 = Pushbutton [package="[SMD]"]
  S2 = Pushbutton [package="[SMD]"]
  R1 = Resistor [tolerance=±5% resistance=220 package="2512 [SMD]"]
  U2 = 7-SEGMENT-4DIGIT [package=7-segment-4digit-youngsun]  # not connected
  U3 = 7-SEGMENT-4DIGIT [package=7-segment-4digit]  # not connected
  U4 = RELAY-2 [package=relay-g5v]

nets:
  N1: Part1.D8, S2.Pin_3, S2.Pin_4
  N2: Part1.D9_PWM, S1.Pin_3, S1.Pin_4
  N3: Part1.D2, U1.VOUT, R1.Pin_1
  N4: Part1.D7, U4.6
  5V: Part1.5V, U1.VCC, R1.Pin_0, U4.2
  GND: Part1.GND, U1.GND, S1.Pin_1, S1.Pin_2, S2.Pin_1, S2.Pin_2, U4.5

notes:
  The temperature sensor has three pins, VCC, Ground and Data. The Data pin must also be connected to VCC via a 4.7k ohm resistor
  In addition to VCC and Ground, the LED display has three pins: DIN, CS, and CLK. I connected these to pins 12, 10 and 11on the Arduino respectively
  The relay module is connected to pin 7, VCC and Ground, and the live terminals connected to the power cable of the extension cable
